# Fritzing sketch WS2812_Matrix_Wiring (saved by Fritzing 0.9.2b)
breadboards: 1

parts:
  Part1 = Arduino Uno (Rev3)
  U1 = mystery part, 4 pins [chip_label=AudioInput]
  U2 = mystery part, 3 pins [chip_label=WS2812]

nets:
  N1: Part1.A0, U1.pin1
  N2: Part1.D6_PWM, U2.pin2
  N3: Part1.5V, U1.pin3, U2.pin3
  N4: Part1.GND, U1.pin2, U2.pin1
